# Fritzing sketch BPL_32 (saved by Fritzing 0.9.3b)
circuit board: 8.17675cm x 5.30193cm

parts:
  I2C = female pin header, 4 pins [form="♀ (female)"]
  BUZZ = Buzzer 12mm [package=buzzer-12mm]
  4CH_RELAY = female pin header, 6 pins [form="♀ (female)"]
  DOOR = Screw terminal - 2 pins [package=THT]
  5V = Screw terminal - 2 pins [package=THT]
  R1 = Resistor [tolerance=±5% resistance=4.7k package=THT]
  PRESSURE = screw terminal, 3 pins
  OW = screw terminal, 3 pins
  30pin_ESP32 = DOIT Esp32 DevKit v1 (30 pins long, 11 pins width) [part_number=ESP32S-PIN30]
  ROT1 = female pin header, 5 pins [form="♀ (female)"]
  Part1 = Adafruit ADS1115 16Bit I2C ADC [part_number="Adafruit #1085"]  # not connected

nets:
  GND: I2C.pin1, BUZZ.2, 4CH_RELAY.pin1, DOOR.pin1, 5V.pin1, PRESSURE.pin1, OW.pin1, 30pin_ESP32.GND, ROT1.pin2
  3.3V: I2C.pin2, 30pin_ESP32.3V3
  N1: I2C.pin3, 30pin_ESP32.D21
  N2: I2C.pin4, 30pin_ESP32.D22
  N3: BUZZ.1, 30pin_ESP32.D18
  N4: 4CH_RELAY.pin2, 30pin_ESP32.TX2
  N5: 4CH_RELAY.pin3, 30pin_ESP32.RX2
  N6: 4CH_RELAY.pin4, 30pin_ESP32.D27
  N7: 4CH_RELAY.pin5, 30pin_ESP32.D19
  5V: 4CH_RELAY.pin6, 5V.pin2, R1.Pin_0, PRESSURE.pin3, OW.pin3, 30pin_ESP32.VIN, ROT1.pin1
  N8: DOOR.pin2, 30pin_ESP32.D26
  N9: R1.Pin_1, OW.pin2, 30pin_ESP32.D23
  N10: PRESSURE.pin2, 30pin_ESP32.VP
  N11: 30pin_ESP32.D32, ROT1.pin3
  N12: 30pin_ESP32.D33, ROT1.pin4
  N13: 30pin_ESP32.D25, ROT1.pin5

notes:
  SDA
  SCL
  3.3
  GND
  5V
  GPIO23
  GPIO18
  GPIO17
  GPIO16
  PUSH
  ROTA
  ROTB
  GPIO36
  GPIO27
  heat
  cool
  fan
  spund
  22
  21
  3.3V
  D
  23
  18
  27
  16
  17
  26
  G
  19

custom parts:
  DOIT Esp32 DevKit v1 (30 pins long, 11 pins width): The DOIT Esp32 DevKit v1 is one of the development board created by DOIT to evaluate the ESP-WROOM-32 module. It is based on the ESP32 microcontroller that boasts Wifi, Bluetooth, Ethernet and Low Power support all in a single chip. (vanepp) made breadboard work, adjusted pin numbering and labels and reduced size of schematic and cleaned up pcb. This chip is 30pins long (2 x15) and 11 pins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
  Adafruit ADS1115 16Bit I2C ADC: For microcontrollers without an analog-to-digital converter or when you want a higher-precision ADC, the ADS1115 provides 16-bit precision at 860 samples/second over I2C. The chip can be configured as 4 single-ended input channels, or two differential channels. As a nice bonus, it even includes a programmable gain amplifier, up to x16, to help boost up smaller single/differential signals to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
