# Fritzing sketch BrewPiLess_ESP32 (saved by Fritzing 0.9.3b)
circuit board: 8.46667cm x 5.64444cm
breadboards: 1

parts:
  J1 = female pin header, 5 pins [form="♀ (female)"]
  M1 = DOIT Esp32 DevKit v1 (30 pins long, 11 pins width) [part_number=ESP32S-PIN30]
  J2 = screw terminal, 3 pins
  R1 = Resistor [tolerance=±5% resistance=4.7k package=THT]
  SG1 = Buzzer 12mm [package=buzzer-12mm-ns-kit]

nets:
  N1: J1.pin1, M1.D32
  N2: J1.pin2, M1.D33
  N3: J1.pin3, M1.D27
  N4: J1.pin4, M1.VIN, J2.pin3, R1.Pin_1
  N5: J1.pin5, M1.GND, J2.pin1
  N6: M1.3V3, SG1.2
  N7: M1.D18, SG1.1
  N8: M1.D23, J2.pin2, R1.Pin_0

custom parts:
  DOIT Esp32 DevKit v1 (30 pins long, 11 pins width): The DOIT Esp32 DevKit v1 is one of the development board created by DOIT to evaluate the ESP-WROOM-32 module. It is based on the ESP32 microcontroller that boasts Wifi, Bluetooth, Ethernet and Low Power support all in a single chip. (vanepp) made breadboard work, adjusted pin numbering and labels and reduced size of schematic and cleaned up pcb. This chip is 30pins long (2 x15) and 11 pins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
